# Fritzing sketch LightDetectionSchematic (saved by Fritzing 0.9.9b)
breadboards: 1

parts:
  Part1 = Arduino Uno (Rev3)
  R1 = Resistor [tolerance=±5% power=0.25 resistance=330 package=THT]
  R2 = Resistor [tolerance=±20% power=0.25 resistance=330 package=THT]
  R3 = Resistor [tolerance=±5% power=0.25 resistance=330 package=THT]
  R4 = Resistor [tolerance=±5% power=0.25 resistance=330 package=THT]
  R5 = Resistor [tolerance=±5% power=0.25 resistance=330 package=THT]
  LED1 = LED - 5mm [color="Red (633nm)" current=0.030 package="5 mm [THT]"]
  LED2 = LED - 5mm [color="Red (633nm)" current=0.030 package="5 mm [THT]"]
  LED3 = LED - 5mm [color="Yellow (595nm)" current=30mA package="5 mm [THT]"]
  LED4 = LED - 5mm [color="Green (570nm)" current=0.030 package="5 mm [THT]"]
  LED5 = LED - 5mm [color="Green (570nm)" current=0.030 package="5 mm [THT]"]
  R6 = Photocell (LDR) [package=THT]
  R7 = Photocell (LDR) [package=THT]
  R8 = Resistor [tolerance=±5% power=0.25W resistance=220 package=THT]
  R9 = Resistor [tolerance=±5% power=0.25 resistance=220 package=THT]

nets:
  N1: Part1.A0, R7.pin_1, R8.Pin_0
  N2: Part1.A1, R6.pin_1, R9.Pin_0
  N3: Part1.D9_PWM, R1.Pin_0
  N4: Part1.D10_PWM/SS, R2.Pin_0
  N5: Part1.D11_PWM/MOSI, R3.Pin_0
  N6: Part1.D12/MISO, R4.Pin_0
  N7: Part1.D13/SCK, R5.Pin_0
  N8: Part1.GND, LED1.cathode, LED2.cathode, LED3.cathode, LED4.cathode, LED5.cathode, R8.Pin_1, R9.Pin_1
  N9: Part1.5V, R6.pin_0, R7.pin_0
  N10: R1.Pin_1, LED5.anode
  N11: R2.Pin_1, LED4.anode
  N12: R3.Pin_1, LED3.anode
  N13: R4.Pin_1, LED2.anode
  N14: R5.Pin_1, LED1.anode
